# Fritzing sketch Sketch in fritzing (saved by Fritzing 0.9.3b)
breadboards: 1

parts:
  U1 = ESP32S-HiLetgo [part_number=ESP32S-HiLetgo]
  R1 = Resistor [tolerance=±5% resistance=220 package=THT]
  LED1 = smd LED [color="Blue (430nm)" package="0805 [SMD]"]
  LED2 = smd LED [color="Green (555nm)" package="0805 [SMD]"]
  HC-SR04_Sensor_1 = HC-SR04 Ultrasonic Distance Sensor
  PIR1 = PIR sensor
  R2 = Resistor [tolerance=±5% resistance=220 package=THT]
  Q1 = TRANSISTOR_NPN [package=to-92]
  J1 = Piezo Speaker
  Mod1 = KY-016 RGB Full Color LED Module [package="Breakout board"]
  R3 = Resistor [tolerance=±5% resistance=220 package=THT]

nets:
  GND: U1.3.3, LED1.anode, LED2.anode, HC-SR04_Sensor_1.GND, PIR1.GND, Q1.C, Mod1.-
  VCC: U1.EN, LED1.cathode, HC-SR04_Sensor_1.VCC, PIR1.VDD, J1.pin2, R3.Pin_0
  N1: U1.GPIO33, R3.Pin_1
  N2: U1.GPIO25, Mod1.R
  N3: U1.GPIO26, Mod1.G
  N4: U1.GPIO27, Mod1.B
  N5: U1.GPIO14, R2.Pin_0
  N6: U1.GND, PIR1.SIG
  N7: U1.GPIO16, R1.Pin_1
  N8: U1.GPIO18, HC-SR04_Sensor_1.TRIG
  N9: U1.GPIO19, HC-SR04_Sensor_1.ECHO
  N10: R1.Pin_0, LED2.cathode
  N11: R2.Pin_1, Q1.B
  N12: Q1.E, J1.pin1

custom parts:
  ESP32S-HiLetgo: HiLetgo ESP-WROOM-32 ESP32 ESP-32S Development Board 2.4GHz Dual-Mode WiFi + Bluetooth Dual Cores Microcontroller The ESP32 integrated with Antenna switches, RF Balun, power amplifiers, low-noise amplifiers, filters, and management modules, and the entire solution occupies the least area of PCB. 2.4 GHz Wi-Fi plus Bluetooth dual-mode chip, with TSMC Ultra-low power consumption 40nm technology,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
  KY-016 RGB Full Color LED Module: KY-016 Arduino full color 5mm RGB LED, different colors can be obtained by mixing the three primary colors.
